# Fritzing sketch sound-camera (saved by Fritzing 0.9.4)
breadboards: 1

parts:
  Raspberry_Pi_1 = Raspberry Pi 3 [part_number=RPI-3-V1.2]
  ADC1 = MCP3008 [package=dil16]  # not connected
  부품1 = Breakout Board for Electret Microphone
  부품2 = Breakout Board for Electret Microphone
  부품3 = Breakout Board for Electret Microphone
  부품4 = Breakout Board for Electret Microphone
  부품5 = Breakout Board for Electret Microphone
  부품6 = Breakout Board for Electret Microphone
  부품7 = Breakout Board for Electret Microphone
  부품8 = Breakout Board for Electret Microphone
  U1 = Graphical LCD 128x64 [package=lcd-g12864]
  부품9 = FTDI Basic Programmer
  S1 = Round Pushbutton
  R1 = Resistor [tolerance=±5% resistance=220 package="2512 [SMD]"]
  J1 = Piezo Speaker

nets:
  N1: Raspberry_Pi_1.3v3, 부품5.AUD, 부품6.AUD, 부품7.AUD, 부품8.AUD, S1.leg1
  GND: Raspberry_Pi_1.GND, 부품5.GND, 부품6.GND, 부품7.GND, 부품8.GND, U1.E, 부품9.POWER, J1.pin1
  N2: Raspberry_Pi_1.GIPO21, S1.leg0, R1.Pin_0
  N3: Raspberry_Pi_1.GIPO20, J1.pin2
  N4: Raspberry_Pi_1.GIPO15, 부품9.TXO
  N5: Raspberry_Pi_1.GIPO14, 부품9.RXI
  N6: Raspberry_Pi_1.5V, U1.K
  GND_2: 부품1.GND, 부품2.GND, 부품3.GND, 부품4.GND, R1.Pin_1
  N7: 부품1.AUD, 부품2.AUD, 부품3.AUD, 부품4.AUD
